# Fritzing sketch Wiring (saved by Fritzing 0.9.3b)
breadboards: 2

parts:
  R1 = Basic Flex Resistor
  R2 = Basic Flex Resistor
  U2 = Vibration Motor- ROB-08449 [package=vibe-motor-10mm]  # not connected
  U3 = Vibration Motor- ROB-08449 [package=vibe-motor-10mm]  # not connected
  U4 = Vibration Motor- ROB-08449 [package=vibe-motor-10mm]  # not connected
  U5 = Vibration Motor- ROB-08449 [package=vibe-motor-10mm]  # not connected
  J1 = Piezo Speaker
  LED2 = smd LED [color="Red (633nm)" package="1206 [SMD]"]  # not connected
  LED3 = smd LED [color="Red (633nm)" package="1206 [SMD]"]  # not connected
  S1 = Round Pushbutton
  R3 = Resistor [tolerance=±5% resistance=220 package="2512 [SMD]"]
  R4 = Resistor [tolerance=±5% resistance=220 package="2512 [SMD]"]  # not connected
  R5 = Resistor [tolerance=±5% resistance=220 package="2512 [SMD]"]  # not connected
  HLK-PM1 = HLK-PM12 [part_number=HLK-PM12]  # not connected
  R6 = Basic Flex Resistor
  R7 = Basic Flex Resistor
  R8 = Resistor [tolerance=±5% resistance=220 package="2010 [SMD]"]
  R9 = Resistor [tolerance=±5% resistance=220 package="2010 [SMD]"]
  R10 = Resistor [tolerance=±5% resistance=220 package="2010 [SMD]"]
  R11 = Resistor [tolerance=±5% resistance=220 package="2010 [SMD]"]
  U1 = ESP32S-HiLetgo [part_number=ESP32S-HiLetgo]

nets:
  N1: R1.pin_1, R2.pin_1, J1.pin1, R6.pin_1, R7.pin_1, U1.GND
  N2: J1.pin2, U1.GPIO4
  N3: S1.leg0, R3.Pin_1
  N4: R8.Pin_0, U1.GPIO35
  N5: R8.Pin_1, R9.Pin_1, R10.Pin_1, R11.Pin_1, U1.3.3
  N6: R9.Pin_0, U1.GPIO34
  N7: R10.Pin_0, U1.GPIO39
  N8: R11.Pin_0, U1.GPIO36

custom parts:
  ESP32S-HiLetgo: HiLetgo ESP-WROOM-32 ESP32 ESP-32S Development Board 2.4GHz Dual-Mode WiFi + Bluetooth Dual Cores Microcontroller The ESP32 integrated with Antenna switches, RF Balun, power amplifiers, low-noise amplifiers, filters, and management modules, and the entire solution occupies the least area of PCB. 2.4 GHz Wi-Fi plus Bluetooth dual-mode chip, with TSMC Ultra-low power consumption 40nm technology,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
